// Logisim project hw.circ as structural Verilog: 5 circuits, main circuit main
module main (
  input  [7:0] in_1,
  output out_2
);

  wire bit_finder_1_out_3, clock_1_out, clock_2_out, reset_out, start_out;
  wire [1:0] joystick_1_x, joystick_1_y;
  wire [2:0] bit_finder_1_out_2;
  wire [3:0] undriven, undriven_2;
  wire [4:0] joystick_controller_out_6, joystick_controller_out_7, joystick_controller_out_8,
       joystick_controller_out_9, joystick_controller_outputs;
  wire [6:0] keyboard_1_data, keyboard_2_data, keyboard_3_data, keyboard_4_data, keyboard_5_data,
       keyboard_6_data;

  Keyboard #(.buflen(1)) keyboard_1 (.data(keyboard_1_data));  // open: clk, re, clr, avail
  Keyboard #(.buflen(1)) keyboard_2 (.data(keyboard_2_data));  // open: clk, re, clr, avail
  Keyboard keyboard_3 (.data(keyboard_3_data));  // open: clk, re, clr, avail
  Keyboard #(.buflen(1)) keyboard_4 (.data(keyboard_4_data));  // open: clk, re, clr, avail
  Keyboard #(.buflen(1)) keyboard_5 (.data(keyboard_5_data));  // open: clk, re, clr, avail
  Keyboard #(.buflen(1)) keyboard_6 (.data(keyboard_6_data));  // open: clk, re, clr, avail
  Joystick #(.bits(2)) joystick_1 (.x(joystick_1_x), .y(joystick_1_y));
  Button start (.out(start_out));
  Button reset (.out(reset_out));
  Clock clock_1 (.out(clock_1_out));
  // Probe on bit_finder_1_out_2
  bit_finder bit_finder_1 (.in_1(in_1), .out_2(bit_finder_1_out_2), .out_3(bit_finder_1_out_3));
  // Probe on bit_finder_1_out_3
  hex_adder hex_adder_1 (.inp1(keyboard_1_data), .inp2(keyboard_2_data), .out1(undriven), .out2(undriven_2));
  Clock clock_2 (.out(clock_2_out));
  joy_controler joystick_controller (
    .joystick_input({joystick_1_y, joystick_1_x}), .CLK(clock_1_out), .start(start_out), .reset(reset_out),
    .Outputs(joystick_controller_outputs), .out_6(joystick_controller_out_6),
    .out_7(joystick_controller_out_7), .out_8(joystick_controller_out_8), .out_9(joystick_controller_out_9));
  Hex_Digit_Display hex_digit_display_1 (.value(undriven));  // open: dp
  Hex_Digit_Display hex_digit_display_2 (.value(undriven_2));  // open: dp
  pattern_rec pattern_recognizer (
    .inp_str(keyboard_3_data), .CLK(clock_2_out),
    .inp_pat({keyboard_6_data, keyboard_5_data, keyboard_4_data}), .is_rec(out_2));
  DotMatrix #(.matrixrows(5)) dotmatrix_1 (
    .col0(joystick_controller_outputs), .col1(joystick_controller_out_6), .col2(joystick_controller_out_7),
    .col3(joystick_controller_out_8), .col4(joystick_controller_out_9));

  // Notes on the sheet:
  //   سوال اول
  //   سوال دوم
  //   سوال سوم
  //   سوال چهارم
  //   pattern
  //   input string
  //   CLk
  //   inp_str
  //   pattern
  //   --------------------------------------------------------------------------------------------------
  //   --------------------------------------------------------------------------------------------------
  //   --------------------------------------------------------------------------------------------------
endmodule

module pattern_rec (
  input  [6:0] inp_str,
  input  CLK,
  input  [20:0] inp_pat,
  output is_rec
);


  // Notes on the sheet:
  //   Inputs
  //   Outputs
endmodule

module joy_controler (
  input  [3:0] joystick_input,
  input  CLK,
  input  start,
  input  reset,
  output [4:0] Outputs,
  output [4:0] out_6,
  output [4:0] out_7,
  output [4:0] out_8,
  output [4:0] out_9
);


  // Notes on the sheet:
  //   Inputs
endmodule

module bit_finder (
  input  [7:0] in_1,
  output [2:0] out_2,
  output out_3
);

  BitFinder #(.\type ("high1")) bitfinder_1 (.in(in_1), .index(out_2), .found(out_3));

  // Notes on the sheet:
  //   Inputs
  //   Outputs
endmodule

module hex_adder (
  input  [6:0] inp1,
  input  [3:0] out1,
  input  [6:0] inp2,
  input  [3:0] out2
);


  // Notes on the sheet:
  //   Inputs
  //   Outputs
endmodule
