// Logisim project hwDone.circ as structural Verilog: 5 circuits, main circuit main
module main (
  input  [7:0] in_1,
  input  \سوال_دوم ,
  output pattern
);

  wire bit_finder_1_out_3, clock_1_out, clock_2_out, reset_out, start_out;
  wire [1:0] joystick_1_p1, joystick_1_p2;
  wire [2:0] bit_finder_1_out_2;
  wire [3:0] hex_adder_1_out1, hex_adder_1_out2;
  wire [4:0] joystick_controller_out_6, joystick_controller_out_7, joystick_controller_out_8,
       joystick_controller_out_9, joystick_controller_outputs;
  wire [6:0] keyboard_1_data, keyboard_2_data, keyboard_3_data, keyboard_4_data, keyboard_5_data,
       keyboard_6_data;

  Keyboard #(.buflen(1)) keyboard_1 (.clr(\سوال_دوم ), .data(keyboard_1_data));  // open: clk, re, avail
  Keyboard #(.buflen(1)) keyboard_2 (.clr(\سوال_دوم ), .data(keyboard_2_data));  // open: clk, re, avail
  Keyboard keyboard_3 (.data(keyboard_3_data));  // open: clk, re, clr, avail
  Keyboard #(.buflen(1)) keyboard_4 (.data(keyboard_4_data));  // open: clk, re, clr, avail
  Keyboard #(.buflen(1)) keyboard_5 (.data(keyboard_5_data));  // open: clk, re, clr, avail
  Keyboard #(.buflen(1)) keyboard_6 (.data(keyboard_6_data));  // open: clk, re, clr, avail
  // Joystick #(.bits(2)) joystick_1: pin names not known; wires that end beside it: joystick_1_p1, joystick_1_p2
  Button start (.out(start_out));
  Button reset (.out(reset_out));
  Clock clock_1 (.out(clock_1_out));
  // Probe on bit_finder_1_out_2
  bit_finder bit_finder_1 (.out_2(bit_finder_1_out_2), .out_3(bit_finder_1_out_3), .in_1(in_1));
  // Probe on bit_finder_1_out_3
  hex_adder hex_adder_1 (
    .out2(hex_adder_1_out2), .out1(hex_adder_1_out1), .inp1(keyboard_1_data), .inp2(keyboard_2_data));  // open: out_7, out_8, out_9, out_4, out_3
  Clock clock_2 (.out(clock_2_out));
  joy_controler joystick_controller (
    .Outputs(joystick_controller_outputs), .out_6(joystick_controller_out_6),
    .out_7(joystick_controller_out_7), .out_8(joystick_controller_out_8), .out_9(joystick_controller_out_9),
    .CLK(clock_1_out), .start(start_out), .reset(reset_out), .joystick_input({joystick_1_p2, joystick_1_p1}));
  Hex_Digit_Display hex_digit_display_1 (.value(hex_adder_1_out1));  // open: dp
  Hex_Digit_Display hex_digit_display_2 (.value(hex_adder_1_out2));  // open: dp
  DotMatrix #(.matrixrows(5)) dotmatrix_1 (
    .col0(joystick_controller_outputs), .col1(joystick_controller_out_6), .col2(joystick_controller_out_7),
    .col3(joystick_controller_out_8), .col4(joystick_controller_out_9));
  pattern_rec pattern_recognizer (
    .CLK(clock_2_out), .inp_pat({keyboard_6_data, keyboard_5_data, keyboard_4_data}),
    .inp_str(keyboard_3_data));  // open: is_rec

  // Notes on the sheet:
  //   سوال اول
  //   سوال سوم
  //   سوال چهارم
  //   pattern
  //   input string
  //   CLk
  //   inp_str
  //   --------------------------------------------------------------------------------------------------
  //   --------------------------------------------------------------------------------------------------
  //   --------------------------------------------------------------------------------------------------
endmodule

module pattern_rec (
  input  [6:0] inp_str,
  input  CLK,
  input  [20:0] inp_pat,
  output is_rec
);

  // Shift_Register #(.length(7)) shift_register_1: pin names not known; wires that end beside it: inp_str
  // Shift_Register #(.length(21)) shift_register_2: pin names not known; wires that end beside it: CLK

  // Notes on the sheet:
  //   Inputs
  //   Outputs
endmodule

module joy_controler (
  input  [3:0] joystick_input,
  input  CLK,
  input  start,
  input  reset,
  output [4:0] Outputs,
  output [4:0] out_6,
  output [4:0] out_7,
  output [4:0] out_8,
  output [4:0] out_9
);


  // Notes on the sheet:
  //   Inputs
endmodule

module bit_finder (
  input  [7:0] in_1,
  output [2:0] out_2,
  output out_3
);

  wire and_1_out, and_2_out, and_3_out, and_4_out, and_5_out, not_1_out, not_2_out, not_3_out, not_4_out,
       not_5_out, not_6_out, not_7_out, not_8_out;

  or or_1 (out_3, in_1[7], in_1[6], in_1[5], in_1[4], in_1[3], in_1[2], in_1[1], in_1[0]);
  not not_1 (not_1_out, in_1[6]);
  and and_1 (and_1_out, in_1[5], not_1_out);
  not not_2 (not_2_out, in_1[4]);
  not not_3 (not_3_out, in_1[6]);
  not not_4 (not_4_out, in_1[6]);
  not not_5 (not_5_out, in_1[4]);
  not not_6 (not_6_out, in_1[2]);
  not not_7 (not_7_out, in_1[4]);
  not not_8 (not_8_out, in_1[5]);
  and and_2 (and_2_out, not_2_out, not_3_out, in_1[3]);
  and and_3 (and_3_out, not_4_out, not_5_out, not_6_out, in_1[1]);
  and and_4 (and_4_out, not_7_out, not_8_out, in_1[2]);
  and and_5 (and_5_out, not_8_out, not_7_out, in_1[3]);
  or or_2 (out_2[0], and_1_out, and_2_out, and_3_out, in_1[7]);
  or or_3 (out_2[1], and_4_out, and_5_out, in_1[6], in_1[7]);
  or or_4 (out_2[2], in_1[4], in_1[5], in_1[6], in_1[7]);

  // Notes on the sheet:
  //   Inputs
  //   Outputs
endmodule

module hex_adder (
  input  [6:0] inp1,
  input  [6:0] inp2,
  output [7:0] out_3,
  output [3:0] out_4,
  output [3:0] out2,
  output [3:0] out1,
  output [3:0] out_7,
  output [3:0] out_8,
  output [7:0] out_9
);

  Adder #(.width(4)) adder_1 (.a(inp2[3:0]), .b({inp2[6], 2'b00, inp2[6]}), .out(out_8));  // open: cin, cout
  Adder #(.width(4)) adder_2 (.a(inp1[3:0]), .b({inp1[6], 2'b00, inp1[6]}), .out(out_4));  // open: cin, cout
  assign out_3 = {{4{1'b0}}, out_4};  // Bit_Extender bit_extender_1
  assign out_9 = {{4{1'b0}}, out_8};  // Bit_Extender bit_extender_2
  Adder adder_3 (.a(out_3), .b(out_9), .out({out1, out2}));  // open: cin, cout

  assign out_7 = {inp2[6], 2'b00, inp2[6]};

  // Notes on the sheet:
  //   Inputs
  //   Outputs
endmodule
